// Digital circuit exportError.dig as structural Verilog
module exportError (
  input  [3:0] A,
  input  [3:0] B,
  input  C_i,
  output [3:0] S,
  output C_o
);

  wire u_add_c_o;

  add #(.applicationType("GHDL"), .externalParameters("/home/hneemann/temp/Digiblock/go/go"), .processType("GHDL")) u_add (
    .c_i(C_i), .a(A[1:0]), .b(B[1:0]), .s(S[1:0]), .c_o(u_add_c_o));
  add #(.applicationType("GHDL"), .externalParameters("/home/hneemann/temp/Digiblock/go/go"), .processType("GHDL")) u_add_2 (
    .c_i(u_add_c_o), .a(A[3:2]), .b(B[3:2]), .s(S[3:2]), .c_o(C_o));

  // Notes on the sheet:
  //   A: default 3
  //   B: default 4
  //   C_i: default 4
endmodule

/* Test case:
A B C_i C_o S 

loop(a,16)
loop(b,16)
  (a) (b) 0 ((a+b)>>4) (a+b)
end loop
end loop
*/

/* Code of add:
LIBRARY ieee;
USE ieee.std_logic_1164.all;
USE ieee.std_logic_unsigned.all;

entity add is
  port (
    c_i: in std_logic;
    a: in std_logic_vector(1 downto 0);
    b: in std_logic_vector(1 downto 0);
    s: out std_logic_vector(1 downto 0);
    c_o: out std_logic );
end add;

architecture add_arch of add is
   signal temp : std_logic_vector(2 downto 0);
begin
   temp <= ('0' & a) + b + c_i;

   s    <= temp(1 downto 0);
   c_o  <= temp(2);
end add_arch;
*/

/* Code of add:
LIBRARY ieee;
USE ieee.std_logic_1164.all;
USE ieee.std_logic_unsigned.all;

entity add is --files are not identical
  port (
    c_i: in std_logic;
    a: in std_logic_vector(1 downto 0);
    b: in std_logic_vector(1 downto 0);
    s: out std_logic_vector(1 downto 0);
    c_o: out std_logic );
end add;

architecture add_arch of add is
   signal temp : std_logic_vector(2 downto 0);
begin
   temp <= ('0' & a) + b + c_i;

   s    <= temp(1 downto 0);
   c_o  <= temp(2);
end add_arch;
*/
