// Digital circuit ghdl3-inc.dig as structural Verilog
module ghdl3_inc (
  input  C_i,
  input  [1:0] A,
  input  [1:0] B,
  output [1:0] S,
  output C_o
);

  add #(.applicationType("GHDL"), .externalParameters("/home/hneemann/temp/Digiblock/go/go"), .processType("GHDL")) u_add (
    .c_i(C_i), .a(A), .b(B), .s(S), .c_o(C_o));

  // Notes on the sheet:
  //   C_i: default 4
  //   A: default 3
  //   B: default 4
endmodule

/* Code of add:
LIBRARY ieee;
USE ieee.std_logic_1164.all;
USE ieee.std_logic_unsigned.all;

entity add is
  port (
    c_i: in std_logic;
    a: in std_logic_vector(1 downto 0);
    b: in std_logic_vector(1 downto 0);
    s: out std_logic_vector(1 downto 0);
    c_o: out std_logic );
end add;

architecture add_arch of add is
   signal temp : std_logic_vector(2 downto 0);
begin
   temp <= ('0' & a) + b + c_i;

   s    <= temp(1 downto 0);
   c_o  <= temp(2);
end add_arch;
*/
