// Digital circuit sevenSeg.dig as structural Verilog
module sevenSeg (
  input  [3:0] D
);

  wire [6:0] u_sevenSeg_led;

  sevenSeg #(.applicationType("GHDL"), .externalParameters("/home/hneemann/temp/Digiblock/go/go"), .processType("GHDL")) u_sevenSeg (
    .d(D), .led(u_sevenSeg_led));
  Seven_Seg seven_seg_1 (
    .a(u_sevenSeg_led[6]), .b(u_sevenSeg_led[5]), .c(u_sevenSeg_led[4]), .d(u_sevenSeg_led[3]),
    .e(u_sevenSeg_led[2]), .f(u_sevenSeg_led[1]), .g(u_sevenSeg_led[0]), .dp(1'b0));
endmodule

/* Code of sevenSeg:
LIBRARY ieee;
USE ieee.std_logic_1164.all;
USE ieee.numeric_std.all;

entity sevenSeg is
  port (
    d  : in  std_logic_vector(3 downto 0);
    led: out std_logic_vector(6 downto 0) 
  );
end sevenSeg;

architecture Behavioral of sevenSeg is
begin
  led <= "1111110" when d="0000" else -- "0"     
         "0110000" when d="0001" else -- "1" 
         "1101101" when d="0010" else -- "2" 
         "1111001" when d="0011" else -- "3" 
         "0110011" when d="0100" else -- "4" 
         "1011011" when d="0101" else -- "5" 
         "1011111" when d="0110" else -- "6" 
         "1110000" when d="0111" else -- "7" 
         "1111111" when d="1000" else -- "8"     
         "1111011" when d="1001" else -- "9" 
         "1110111" when d="1010" else -- "A"
         "0011111" when d="1011" else -- "b"
         "1001110" when d="1100" else -- "C"
         "0111101" when d="1101" else -- "d"
         "1001111" when d="1110" else -- "E"
         "1000111" when d="1111" else -- "F"
         "0000000"; -- off
end Behavioral;
*/
