// Digital circuit verilog3-inc.dig as structural Verilog
module verilog3_inc (
  input  C_i,
  input  [1:0] A,
  input  [1:0] B,
  output [1:0] S,
  output C_o
);

  add #(.applicationType("IVERILOG"), .externalParameters("/home/hneemann/temp/Digiblock/go/go"), .processType("GHDL")) u_add (
    .c_i(C_i), .a(A), .b(B), .s(S), .c_o(C_o));

  // Notes on the sheet:
  //   C_i: default 4
  //   A: default 3
  //   B: default 4
endmodule

/* Code of add:
module add
(
    input [1:0] a,
    input [1:0] b,
    input c_i,
    output [1:0] s,
    output c_o
);
   wire [2:0] temp;

   assign temp = a + b + c_i;
   assign s = temp [1:0];
   assign c_o = temp[2];
endmodule
*/
